# Fritzing sketch greenhouse (saved by Fritzing 0.9.2b)
circuit board: 8.46667cm x 5.64444cm
breadboards: 1

parts:
  Part1 = Arduino Mega 2560 (Rev3)
  R2 = Resistor [tolerance=±5% resistance=1k package="1206 [SMD]"]
  Q1 = PNP-Transistor [package="TO92 [THT]"]
  RHT1 = Humidity and Temperature Sensor RHT03
  M1 = DC Motor
  U1 = RELAY [package=relay-g5q]
  R1 = Resistor [tolerance=±5% resistance=4.7k package="1206 [SMD]"]

nets:
  N1: Part1.GND, Q1.B
  5V: Part1.5V, RHT1.Vcc
  N2: Part1.VIN, RHT1.GND_2, U1.NC
  N3: Part1.D2_PWM, R1.Pin_1
  N4: Part1.D7_PWM, R2.Pin_1
  N5: R2.Pin_0, Q1.C
  N6: Q1.E, U1.COIL1
  N7: M1.pin_1, U1.COIL2
  N8: M1.pin_2, U1.MAIN
